# Fritzing sketch Schema (saved by Fritzing 0.9.3b)
breadboards: 1

parts:
  Power_plug_(5V) = Power plug
  C1 = Electrolytic Capacitor [capacitance=1mF package="100 mil [THT, electrolytic]"]
  R1 = Resistor [tolerance=±5% resistance=330 package=THT]
  LED2 = LED - 5mm [color="Red (633nm)" package="5 mm [THT]"]
  R2 = Resistor [tolerance=±5% resistance=330 package=THT]
  Node_MCU_/_ESP8266 = NodeMCU V1.0
  Neopixel = 24 NeoPixel Ring [part_number=1586]

nets:
  GND: Power_plug_(5V).GND, C1.-, R1.Pin_1, Node_MCU_/_ESP8266.GND, Neopixel.GND
  VCC: Power_plug_(5V).VCC, C1.+, Neopixel.VDD
  N1: R1.Pin_0, LED2.cathode
  N2: LED2.anode, Node_MCU_/_ESP8266.D7
  N3: R2.Pin_0, Neopixel.IN
  N4: R2.Pin_1, Node_MCU_/_ESP8266.D5

custom parts:
  NodeMCU V1.0: ESP8266 based NodeMCU
  24 NeoPixel Ring: 24 ultra bright smart LED NeoPixels are arranged in a circle with 2.6" (66mm) outer diameter. The rings are 'chainable' - connect the output pin of one to the input pin of another. Use only one microcontroller pin to control as many as you can chain together! Each LED is addressable as the driver chip is inside the LED. Each one has ~18mA constant current drive so the color will be very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
